// Logisim project 4자리저장.circ as structural Verilog: 3 circuits, main circuit main
module main (
);

  wire _0_out, _1_out, _2_out, _3_out, _4_out, _5_out, _6_out, _7_out, _8_out, _9_out, button_1_out,
       d_ff_1_q, d_ff_2_q, d_ff_3_q, d_ff_4_q, or_1_out;
  wire [3:0] \n4자리_저장_1_out_16 , \n4자리_저장_1_out_17 , \n4자리_저장_1_out_18 , \n4자리_저장_1_out_19 ;

  or or_1 (or_1_out, _1_out, _2_out, _3_out, _4_out, _5_out, _6_out, _7_out, _8_out, _9_out, _0_out);
  Button _1 (.out(_1_out));
  Button _2 (.out(_2_out));
  Button _3 (.out(_3_out));
  Button _4 (.out(_4_out));
  Button _5 (.out(_5_out));
  Button _6 (.out(_6_out));
  Button _7 (.out(_7_out));
  Button _8 (.out(_8_out));
  Button _9 (.out(_9_out));
  Button _0 (.out(_0_out));
  Button button_1 (.out(button_1_out));
  D_Flip_Flop d_ff_1 (.clk(or_1_out), .D(1'b1), .Q(d_ff_1_q), .reset(button_1_out));  // open: Qn, preset, en
  D_Flip_Flop d_ff_2 (.clk(or_1_out), .D(d_ff_1_q), .Q(d_ff_2_q), .reset(button_1_out));  // open: Qn, preset, en
  D_Flip_Flop d_ff_3 (.clk(or_1_out), .D(d_ff_2_q), .Q(d_ff_3_q), .reset(button_1_out));  // open: Qn, preset, en
  \_4자리_저장  \u_4자리_저장_1  (
    .in_5(_1_out), .in_6(_2_out), .in_7(_3_out), .in_8(_4_out), .in_9(_5_out), .in_10(_6_out),
    .in_11(_7_out), .in_12(_8_out), .in_13(_9_out), .in_14(_0_out), .in_15(button_1_out), .in_1(d_ff_1_q),
    .out_16(\n4자리_저장_1_out_16 ), .in_2(d_ff_2_q), .out_17(\n4자리_저장_1_out_17 ), .in_3(d_ff_3_q),
    .out_18(\n4자리_저장_1_out_18 ), .in_4(d_ff_4_q), .out_19(\n4자리_저장_1_out_19 ));
  D_Flip_Flop d_ff_4 (.clk(or_1_out), .D(d_ff_3_q), .Q(d_ff_4_q), .reset(button_1_out));  // open: Qn, preset, en
  Hex_Digit_Display hex_digit_display_1 (.value(\n4자리_저장_1_out_16 ));  // open: dp
  Hex_Digit_Display hex_digit_display_2 (.value(\n4자리_저장_1_out_17 ));  // open: dp
  Hex_Digit_Display hex_digit_display_3 (.value(\n4자리_저장_1_out_18 ));  // open: dp
  Hex_Digit_Display hex_digit_display_4 (.value(\n4자리_저장_1_out_19 ));  // open: dp
endmodule

module _2x1_encoder (
  input  in_1,
  input  in_2,
  input  in_3,
  input  in_4,
  input  in_5,
  input  in_6,
  input  in_7,
  input  in_8,
  input  in_9,
  input  in_10,
  input  in_11,
  input  in_12,
  output [3:0] out_13,
  output out_14,
  output out_15,
  output out_16,
  output out_17,
  output out_18,
  output out_19,
  output out_20,
  output out_21,
  output out_22,
  output out_23
);

  wire controlled_buffer_1_out, controlled_buffer_2_out, controlled_buffer_3_out, controlled_buffer_4_out,
       d_ff_2_q, not_1_out, or_1_out, or_2_out, or_3_out, or_4_out, or_5_out;
  wire [3:0] d_ff_5_q;

  and and_1 (out_14, in_2, in_1);
  and and_2 (out_15, in_3, in_1);
  and and_3 (out_16, in_4, in_1);
  and and_4 (out_17, in_5, in_1);
  and and_5 (out_18, in_6, in_1);
  and and_6 (out_19, in_7, in_1);
  and and_7 (out_20, in_8, in_1);
  and and_8 (out_21, in_9, in_1);
  and and_9 (out_22, in_10, in_1);
  and and_10 (out_23, in_11, in_1);
  or or_1 (or_1_out, out_22, out_21);
  assign controlled_buffer_1_out = not_1_out ? or_1_out : 1'bz;  // Controlled_Buffer controlled_buffer_1
  or or_2 (or_2_out, out_20, out_19, out_18, out_17);
  D_Flip_Flop d_ff_1 (
    .clk(controlled_buffer_1_out), .D(controlled_buffer_1_out), .Q(d_ff_5_q[3]), .reset(in_12));  // open: Qn, preset, en
  assign controlled_buffer_2_out = not_1_out ? or_2_out : 1'bz;  // Controlled_Buffer controlled_buffer_2
  D_Flip_Flop d_ff_2 (.clk(out_23), .D(out_23), .Q(d_ff_2_q), .reset(in_12));  // open: Qn, preset, en
  D_Flip_Flop d_ff_3 (
    .clk(controlled_buffer_2_out), .D(controlled_buffer_2_out), .Q(d_ff_5_q[2]), .reset(in_12));  // open: Qn, preset, en
  or or_3 (or_3_out, out_20, out_19, out_16, out_15);
  assign controlled_buffer_3_out = not_1_out ? or_3_out : 1'bz;  // Controlled_Buffer controlled_buffer_3
  D_Flip_Flop d_ff_4 (
    .clk(controlled_buffer_3_out), .D(controlled_buffer_3_out), .Q(d_ff_5_q[1]), .reset(in_12));  // open: Qn, preset, en
  or or_4 (or_4_out, out_22, out_20, out_18, out_16, out_14);
  assign controlled_buffer_4_out = not_1_out ? or_4_out : 1'bz;  // Controlled_Buffer controlled_buffer_4
  D_Flip_Flop d_ff_5 (
    .clk(controlled_buffer_4_out), .D(controlled_buffer_4_out), .Q(d_ff_5_q[0]), .reset(in_12));  // open: Qn, preset, en
  not not_1 (not_1_out, or_5_out);
  or or_5 (or_5_out, d_ff_5_q[0], d_ff_5_q[1], d_ff_5_q[2], d_ff_5_q[3], d_ff_2_q);
  assign out_13 = or_5_out ? d_ff_5_q : 4'bz;  // Controlled_Buffer controlled_buffer_5
endmodule

module \_4자리_저장  (
  input  in_1,
  input  in_2,
  input  in_3,
  input  in_4,
  input  in_5,
  input  in_6,
  input  in_7,
  input  in_8,
  input  in_9,
  input  in_10,
  input  in_11,
  input  in_12,
  input  in_13,
  input  in_14,
  input  in_15,
  output [3:0] out_16,
  output [3:0] out_17,
  output [3:0] out_18,
  output [3:0] out_19
);

  wire n2x1_encoder_1_out_14, n2x1_encoder_1_out_15, n2x1_encoder_1_out_16, n2x1_encoder_1_out_17,
       n2x1_encoder_1_out_18, n2x1_encoder_1_out_19, n2x1_encoder_1_out_20, n2x1_encoder_1_out_21,
       n2x1_encoder_1_out_22, n2x1_encoder_1_out_23, n2x1_encoder_2_out_14, n2x1_encoder_2_out_15,
       n2x1_encoder_2_out_16, n2x1_encoder_2_out_17, n2x1_encoder_2_out_18, n2x1_encoder_2_out_19,
       n2x1_encoder_2_out_20, n2x1_encoder_2_out_21, n2x1_encoder_2_out_22, n2x1_encoder_2_out_23,
       n2x1_encoder_3_out_14, n2x1_encoder_3_out_15, n2x1_encoder_3_out_16, n2x1_encoder_3_out_17,
       n2x1_encoder_3_out_18, n2x1_encoder_3_out_19, n2x1_encoder_3_out_20, n2x1_encoder_3_out_21,
       n2x1_encoder_3_out_22, n2x1_encoder_3_out_23;

  _2x1_encoder u_2x1_encoder_1 (
    .in_2(in_5), .in_3(in_6), .in_4(in_7), .in_5(in_8), .in_6(in_9), .in_7(in_10), .in_8(in_11),
    .in_9(in_12), .in_10(in_13), .in_11(in_14), .in_12(in_15), .out_14(n2x1_encoder_1_out_14),
    .out_15(n2x1_encoder_1_out_15), .out_16(n2x1_encoder_1_out_16), .out_17(n2x1_encoder_1_out_17),
    .out_18(n2x1_encoder_1_out_18), .out_19(n2x1_encoder_1_out_19), .out_20(n2x1_encoder_1_out_20),
    .out_21(n2x1_encoder_1_out_21), .out_22(n2x1_encoder_1_out_22), .out_23(n2x1_encoder_1_out_23),
    .in_1(in_1), .out_13(out_16));
  _2x1_encoder u_2x1_encoder_2 (
    .in_2(n2x1_encoder_1_out_14), .in_3(n2x1_encoder_1_out_15), .in_4(n2x1_encoder_1_out_16),
    .in_5(n2x1_encoder_1_out_17), .in_6(n2x1_encoder_1_out_18), .in_7(n2x1_encoder_1_out_19),
    .in_8(n2x1_encoder_1_out_20), .in_9(n2x1_encoder_1_out_21), .in_10(n2x1_encoder_1_out_22),
    .in_11(n2x1_encoder_1_out_23), .in_12(in_15), .out_14(n2x1_encoder_2_out_14),
    .out_15(n2x1_encoder_2_out_15), .out_16(n2x1_encoder_2_out_16), .out_17(n2x1_encoder_2_out_17),
    .out_18(n2x1_encoder_2_out_18), .out_19(n2x1_encoder_2_out_19), .out_20(n2x1_encoder_2_out_20),
    .out_21(n2x1_encoder_2_out_21), .out_22(n2x1_encoder_2_out_22), .out_23(n2x1_encoder_2_out_23),
    .in_1(in_2), .out_13(out_17));
  _2x1_encoder u_2x1_encoder_3 (
    .in_2(n2x1_encoder_2_out_14), .in_3(n2x1_encoder_2_out_15), .in_4(n2x1_encoder_2_out_16),
    .in_5(n2x1_encoder_2_out_17), .in_6(n2x1_encoder_2_out_18), .in_7(n2x1_encoder_2_out_19),
    .in_8(n2x1_encoder_2_out_20), .in_9(n2x1_encoder_2_out_21), .in_10(n2x1_encoder_2_out_22),
    .in_11(n2x1_encoder_2_out_23), .in_12(in_15), .out_14(n2x1_encoder_3_out_14),
    .out_15(n2x1_encoder_3_out_15), .out_16(n2x1_encoder_3_out_16), .out_17(n2x1_encoder_3_out_17),
    .out_18(n2x1_encoder_3_out_18), .out_19(n2x1_encoder_3_out_19), .out_20(n2x1_encoder_3_out_20),
    .out_21(n2x1_encoder_3_out_21), .out_22(n2x1_encoder_3_out_22), .out_23(n2x1_encoder_3_out_23),
    .in_1(in_3), .out_13(out_18));
  _2x1_encoder u_2x1_encoder_4 (
    .in_2(n2x1_encoder_3_out_14), .in_3(n2x1_encoder_3_out_15), .in_4(n2x1_encoder_3_out_16),
    .in_5(n2x1_encoder_3_out_17), .in_6(n2x1_encoder_3_out_18), .in_7(n2x1_encoder_3_out_19),
    .in_8(n2x1_encoder_3_out_20), .in_9(n2x1_encoder_3_out_21), .in_10(n2x1_encoder_3_out_22),
    .in_11(n2x1_encoder_3_out_23), .in_12(in_15), .in_1(in_4), .out_13(out_19));  // open: out_14, out_15, out_16, out_17, out_18, out_19, out_20, out_21, out_22, out_23
endmodule
