// Logisim project 7-Segment Display Practice.circ as structural Verilog: 1 circuit, main circuit main
module main (
);

  wire and_1_out, and_2_out, and_3_out, and_4_out, and_5_out, and_6_out, and_7_out, and_8_out, button_1_out,
       button_2_out, not_1_out, not_2_out, not_3_out, not_4_out, not_5_out, not_6_out, or_1_out, or_2_out,
       or_3_out, or_4_out, or_5_out, or_6_out, or_7_out;
  wire [7:0] counter_1_q;

  Button button_1 (.out(button_1_out));
  Button button_2 (.out(button_2_out));
  not not_1 (not_1_out, counter_1_q[2]);
  not not_2 (not_2_out, counter_1_q[3]);
  and and_1 (and_1_out, not_1_out, not_2_out, counter_1_q[1]);
  and and_2 (and_2_out, counter_1_q[2], not_2_out, not_3_out);
  Counter counter_1 (.Q(counter_1_q), .clk(button_1_out), .clr(button_2_out));  // open: load, D, count, carry
  not not_3 (not_3_out, counter_1_q[1]);
  and and_3 (and_3_out, counter_1_q[0], counter_1_q[2], not_3_out);
  or or_1 (or_1_out, and_2_out, and_1_out, counter_1_q[3], and_5_out);
  not not_4 (not_4_out, counter_1_q[0]);
  not not_5 (not_5_out, counter_1_q[1]);
  not not_6 (not_6_out, counter_1_q[2]);
  and and_4 (and_4_out, counter_1_q[1], counter_1_q[0]);
  and and_5 (and_5_out, counter_1_q[1], not_4_out);
  and and_6 (and_6_out, not_4_out, not_5_out);
  and and_7 (and_7_out, not_4_out, not_6_out);
  or or_2 (or_2_out, not_6_out, and_6_out, and_4_out);
  and and_8 (and_8_out, counter_1_q[0], counter_1_q[2]);
  or or_3 (or_3_out, counter_1_q[3], and_8_out, counter_1_q[1], and_7_out);
  or or_4 (or_4_out, and_6_out, counter_1_q[2], counter_1_q[3]);
  _7_Segment_Display u_7_segment_display_1 (
    .g(or_1_out), .f(or_4_out), .a(or_3_out), .b(or_2_out), .e(or_7_out), .d(or_6_out), .c(or_5_out));  // open: dp
  or or_5 (or_5_out, counter_1_q[3], counter_1_q[2], not_5_out, and_4_out);
  or or_6 (or_6_out, and_7_out, and_5_out, and_1_out, and_3_out);
  or or_7 (or_7_out, and_5_out, and_7_out);
endmodule
