// Logisim project Mod-4 D FilpFlop.circ as structural Verilog: 1 circuit, main circuit main
module main (
  input  in_1
);

  wire and_1_out, and_2_out, and_3_out, and_4_out, and_5_out, clock_1_out, d_ff_1_qn, d_ff_2_qn, not_1_out,
       or_1_out, or_2_out;
  wire [1:0] d_ff_2_q;

  not not_1 (not_1_out, in_1);
  and and_1 (and_1_out, d_ff_2_q[1], not_1_out);
  and and_2 (and_2_out, d_ff_2_q[1], d_ff_2_qn);
  and and_3 (and_3_out, in_1, d_ff_2_q[0], d_ff_1_qn);
  and and_4 (and_4_out, d_ff_2_q[0], not_1_out);
  and and_5 (and_5_out, in_1, d_ff_2_qn);
  or or_1 (or_1_out, and_1_out, and_2_out, and_3_out);
  or or_2 (or_2_out, and_4_out, and_5_out);
  Clock clock_1 (.out(clock_1_out));
  D_Flip_Flop d_ff_1 (.clk(clock_1_out), .D(or_1_out), .Q(d_ff_2_q[1]), .Qn(d_ff_1_qn));  // open: preset, en, reset
  D_Flip_Flop d_ff_2 (.clk(clock_1_out), .D(or_2_out), .Q(d_ff_2_q[0]), .Qn(d_ff_2_qn));  // open: preset, en, reset
  Hex_Digit_Display hex_digit_display_1 (.value({2'b00, d_ff_2_q}));  // open: dp
endmodule
