// Logisim project 레지스터.circ as structural Verilog: 1 circuit, main circuit main
module main (
  input  [1:0] in_1,
  input  [1:0] in_2,
  input  [7:0] in_3,
  input  in_4,
  input  in_5
);

  wire clock_1_out, decoder_1_out0, decoder_1_out1, decoder_1_out2, decoder_1_out3, decoder_2_out0,
       decoder_2_out1, decoder_2_out2, decoder_2_out3, nor_1_out, not_1_out;
  wire [3:0] register_1_q, register_1_q_2, register_3_q, register_3_q_2;
  wire [7:0] controlled_buffer_1_out, register_2_q, register_4_q;

  not not_1 (not_1_out, in_5);
  assign controlled_buffer_1_out = in_4 ? in_3 : 8'bz;  // Controlled_Buffer controlled_buffer_1
  Decoder #(.select(2), .disabled(0)) decoder_1 (
    .out0(decoder_1_out0), .out1(decoder_1_out1), .out2(decoder_1_out2), .out3(decoder_1_out3), .sel(in_1),
    .en(not_1_out));
  Clock clock_1 (.out(clock_1_out));
  Hex_Digit_Display hex_digit_display_1 (.value(register_1_q));  // open: dp
  Hex_Digit_Display hex_digit_display_2 (.value(register_1_q_2));  // open: dp
  Register register_1 (
    .D(controlled_buffer_1_out), .en(decoder_1_out0), .Q({register_1_q_2, register_1_q}), .clk(clock_1_out));  // open: clr
  Register register_2 (
    .D(controlled_buffer_1_out), .en(decoder_1_out1), .Q(register_2_q), .clk(clock_1_out));  // open: clr
  Register register_3 (
    .D(controlled_buffer_1_out), .en(decoder_1_out2), .Q({register_3_q_2, register_3_q}), .clk(clock_1_out));  // open: clr
  Register register_4 (
    .D(controlled_buffer_1_out), .en(decoder_1_out3), .Q(register_4_q), .clk(clock_1_out));  // open: clr
  nor nor_1 (nor_1_out, in_4, in_5);
  Hex_Digit_Display hex_digit_display_3 (.value(register_2_q[3:0]));  // open: dp
  Hex_Digit_Display hex_digit_display_4 (.value(register_2_q[7:4]));  // open: dp
  assign controlled_buffer_1_out = decoder_2_out0 ? {register_1_q_2, register_1_q} : 8'bz;  // Controlled_Buffer controlled_buffer_2
  Decoder #(.select(2), .disabled(0)) decoder_2 (
    .out0(decoder_2_out0), .out1(decoder_2_out1), .out2(decoder_2_out2), .out3(decoder_2_out3), .sel(in_2),
    .en(nor_1_out));
  Hex_Digit_Display hex_digit_display_5 (.value(register_3_q_2));  // open: dp
  Hex_Digit_Display hex_digit_display_6 (.value(register_3_q));  // open: dp
  assign controlled_buffer_1_out = decoder_2_out1 ? register_2_q : 8'bz;  // Controlled_Buffer controlled_buffer_3
  assign controlled_buffer_1_out = decoder_2_out2 ? {register_3_q_2, register_3_q} : 8'bz;  // Controlled_Buffer controlled_buffer_4
  assign controlled_buffer_1_out = decoder_2_out3 ? register_4_q : 8'bz;  // Controlled_Buffer controlled_buffer_5
  Hex_Digit_Display hex_digit_display_7 (.value(register_4_q[7:4]));  // open: dp
  Hex_Digit_Display hex_digit_display_8 (.value(register_4_q[3:0]));  // open: dp
endmodule
