// Logisim project 비밀번호 1230.circ as structural Verilog
module main (
);

  wire button_1_out, button_2_out, button_3_out, button_4_out, button_5_out, button_6_out, button_7_out,
       button_8_out, button_9_out, button_10_out, button_11_out, button_12_out, d_ff_1_q, d_ff_2_q,
       d_ff_2_qn, d_ff_3_q, d_ff_4_q, d_ff_5_q, not_1_out, or_1_out;
  wire [3:0] controlled_buffer_1_out, controlled_buffer_2_out, controlled_buffer_3_out, multiplexer_1_out,
       multiplexer_2_out, multiplexer_3_out, undriven, undriven_2, undriven_3;

  D_Flip_Flop d_ff_1 (.clk(button_4_out), .D(d_ff_2_qn), .Q(d_ff_1_q));  // open: Qn, preset, en, reset
  not not_1 (not_1_out, button_4_out);
  Button button_1 (.out(button_1_out));
  Button button_2 (.out(button_2_out));
  Button button_3 (.out(button_3_out));
  Button button_4 (.out(button_4_out));
  D_Flip_Flop d_ff_2 (.clk(not_1_out), .D(d_ff_1_q), .Q(d_ff_2_q), .Qn(d_ff_2_qn));  // open: preset, en, reset
  Button button_5 (.out(button_5_out));
  Button button_6 (.out(button_6_out));
  Button button_7 (.out(button_7_out));
  Button button_8 (.out(button_8_out));
  Button button_9 (.out(button_9_out));
  Button button_10 (.out(button_10_out));
  Button button_11 (.out(button_11_out));
  Button button_12 (.out(button_12_out));
  or or_1 (or_1_out, button_9_out, button_10_out, button_3_out, button_7_out, button_8_out, button_2_out, button_5_out, button_6_out, button_1_out, button_11_out);
  D_Flip_Flop d_ff_3 (.clk(or_1_out), .D(d_ff_4_q), .Q(d_ff_3_q), .reset(button_12_out));  // open: Qn, preset, en
  D_Flip_Flop d_ff_4 (.clk(or_1_out), .D(d_ff_5_q), .Q(d_ff_4_q), .reset(button_12_out));  // open: Qn, preset, en
  D_Flip_Flop d_ff_5 (.clk(or_1_out), .D(1'b1), .Q(d_ff_5_q), .reset(button_12_out));  // open: Qn, preset, en
  Hex_Digit_Display hex_digit_display_1 (.value(multiplexer_1_out));  // open: dp
  Multiplexer #(.width(4), .enable("false")) multiplexer_1 (
    .in0(controlled_buffer_2_out), .out(multiplexer_1_out), .sel(d_ff_2_q));  // open: in1
  assign controlled_buffer_1_out = d_ff_4_q ? undriven_2 : 4'bz;  // Controlled_Buffer controlled_buffer_1
  assign controlled_buffer_2_out = d_ff_5_q ? undriven : 4'bz;  // Controlled_Buffer controlled_buffer_2
  Hex_Digit_Display hex_digit_display_2 (.value(multiplexer_3_out));  // open: dp
  Hex_Digit_Display hex_digit_display_3 (.value(multiplexer_2_out));  // open: dp
  Multiplexer #(.width(4), .enable("false")) multiplexer_2 (
    .in0(controlled_buffer_3_out), .out(multiplexer_2_out), .sel(d_ff_2_q));  // open: in1
  Multiplexer #(.width(4), .enable("false")) multiplexer_3 (
    .in0(controlled_buffer_1_out), .out(multiplexer_3_out), .sel(d_ff_2_q));  // open: in1
  assign controlled_buffer_3_out = d_ff_3_q ? undriven_3 : 4'bz;  // Controlled_Buffer controlled_buffer_3
endmodule
