// Logisim project 시계.circ as structural Verilog: 5 circuits, main circuit main
module main (
);

  wire and_1_out, and_2_out, and_3_out, and_4_out, and_5_out, and_6_out, and_7_out, and_8_out, and_9_out,
       and_10_out, and_11_out, button_1_out, button_2_out, button_3_out, button_4_out, button_5_out,
       clock_1_out, controlled_buffer_1_out, controlled_buffer_2_out, controlled_buffer_3_out, d_ff_1_q,
       d_ff_2_q, d_ff_2_qn, d_ff_3_q, d_ff_4_q, d_ff_4_qn, n4bit_gle_1_out_11, n4bit_gle_2_out_11,
       n4bit_gle_3_out_11, n4bit_gle_4_out_11, n74162_3__15__tc, n74162_4__15__tc, n74162_6__15__tc,
       n74162_8__15__tc, n74162_10__15__tc, nand_1_out, nand_2_out, nand_3_out, nand_4_out, nand_5_out,
       nor_1_out, nor_2_out, nor_3_out, nor_4_out, nor_5_out, nor_6_out, nor_7_out, not_1_out, not_2_out,
       not_3_out, not_4_out, not_5_out, not_6_out, not_7_out, not_8_out, not_9_out, not_10_out, or_1_out,
       or_2_out, or_3_out, or_4_out, or_5_out, or_6_out, t_ff_1_q, t_ff_1_qn, xnor_1_out;
  wire [3:0] multiplexer_1_out, multiplexer_2_out, multiplexer_3_out, multiplexer_4_out, multiplexer_5_out,
       multiplexer_6_out, n74162_1__14__q0, n74162_2__14__q0, n74162_3__14__q0, n74162_4__14__q0,
       n74162_5__14__q0, n74162_6__14__q0, n74162_7__14__q0, n74162_8__14__q0, n74162_9__14__q0,
       n74162_10__14__q0;

  or or_1 (or_1_out, t_ff_1_qn, t_ff_1_q);
  LED led_1 (.in(t_ff_1_q));
  LED led_2 (.in(and_1_out));
  not not_1 (not_1_out, and_1_out);
  Clock clock_1 (.out(clock_1_out));
  not not_2 (not_2_out, and_1_out);
  assign controlled_buffer_1_out = not_2_out ? clock_1_out : 1'bz;  // Controlled_Buffer controlled_buffer_1
  not not_3 (not_3_out, controlled_buffer_1_out);
  T_Flip_Flop t_ff_1 (
    .clk(controlled_buffer_3_out), .T(or_1_out), .Q(t_ff_1_q), .Qn(t_ff_1_qn));  // open: preset, reset, en
  not not_4 (not_4_out, t_ff_1_q);
  Button button_1 (.out(button_1_out));
  Button button_2 (.out(button_2_out));
  assign controlled_buffer_2_out = not_4_out ? button_2_out : 1'bz;  // Controlled_Buffer controlled_buffer_2
  Button button_3 (.out(button_3_out));
  Button button_4 (.out(button_4_out));
  Button button_5 (.out(button_5_out));
  nor nor_1 (nor_1_out, clock_1_out, and_1_out);
  and and_1 (and_1_out, xnor_1_out, d_ff_2_q);
  not not_5 (not_5_out, controlled_buffer_2_out);
  D_Flip_Flop #(.trigger("high")) d_ff_1 (.clk(not_3_out), .D(d_ff_4_qn), .Q(d_ff_1_q));  // open: Qn, preset, en, reset
  LED led_3 (.in(and_10_out));
  assign controlled_buffer_3_out = not_1_out ? button_1_out : 1'bz;  // Controlled_Buffer controlled_buffer_3
  not not_6 (not_6_out, nand_2_out);
  D_Flip_Flop #(.trigger("high")) d_ff_2 (
    .clk(controlled_buffer_2_out), .D(d_ff_3_q), .Q(d_ff_2_q), .Qn(d_ff_2_qn));  // open: preset, en, reset
  D_Flip_Flop #(.trigger("high")) d_ff_3 (.clk(not_5_out), .D(d_ff_2_qn), .Q(d_ff_3_q));  // open: Qn, preset, en, reset
  D_Flip_Flop #(.trigger("high")) d_ff_4 (
    .clk(controlled_buffer_1_out), .D(d_ff_1_q), .Q(d_ff_4_q), .Qn(d_ff_4_qn));  // open: preset, en, reset
  nand nand_1 (nand_1_out, n74162_3__14__q0[0], n74162_3__14__q0[1], n74162_1__14__q0[1]);
  and and_2 (and_2_out, t_ff_1_q, button_3_out);
  and and_3 (and_3_out, t_ff_1_q, button_4_out);
  nand nand_2 (nand_2_out, n74162_2__14__q0[1], and_8_out);
  nor nor_2 (nor_2_out, not_6_out, and_4_out, nor_1_out);
  and and_4 (and_4_out, n74162_4__15__tc, and_5_out);
  xnor xnor_1 (xnor_1_out, d_ff_1_q, d_ff_4_q);
  Hex_Digit_Display hex_digit_display_1 (.value(multiplexer_1_out));  // open: dp
  Multiplexer #(.width(4), .enable("false")) multiplexer_1 (
    .in0(n74162_2__14__q0), .in1(n74162_1__14__q0), .out(multiplexer_1_out), .sel(t_ff_1_q));
  _74162 u_74162_1 (
    ._1__nMR(nand_1_out), ._2__CP(and_2_out), ._7__CEP(n74162_3__15__tc), ._14__Q0(n74162_1__14__q0[0]),
    ._13__Q1(n74162_1__14__q0[1]), ._12__Q2(n74162_1__14__q0[2]), ._11__O3(n74162_1__14__q0[3]),
    ._10__CET(n74162_3__15__tc));  // open: _3__D0, _4__D1, _5__D2, _6__D3, _8__GND, _16__Vcc, _15__TC, _9__nPE
  _74162 u_74162_2 (
    ._1__nMR(nand_2_out), ._2__CP(nor_2_out), ._7__CEP(or_2_out), ._14__Q0(n74162_2__14__q0[0]),
    ._13__Q1(n74162_2__14__q0[1]), ._12__Q2(n74162_2__14__q0[2]), ._11__O3(n74162_2__14__q0[3]),
    ._10__CET(or_2_out));  // open: _3__D0, _4__D1, _5__D2, _6__D3, _8__GND, _16__Vcc, _15__TC, _9__nPE
  or or_2 (or_2_out, n74162_4__15__tc, and_1_out);
  and and_5 (and_5_out, button_3_out, and_1_out);
  and and_6 (and_6_out, button_4_out, and_1_out);
  and and_7 (and_7_out, button_5_out, and_1_out);
  Hex_Digit_Display hex_digit_display_2 (.value(multiplexer_2_out));  // open: dp
  Multiplexer #(.width(4), .enable("false")) multiplexer_2 (
    .in0(n74162_4__14__q0), .in1(n74162_3__14__q0), .out(multiplexer_2_out), .sel(t_ff_1_q));
  _74162 u_74162_3 (
    ._1__nMR(nand_1_out), ._2__CP(and_2_out), ._7__CEP(1'b1), ._15__TC(n74162_3__15__tc),
    ._14__Q0(n74162_3__14__q0[0]), ._13__Q1(n74162_3__14__q0[1]), ._12__Q2(n74162_3__14__q0[2]),
    ._11__O3(n74162_3__14__q0[3]), ._10__CET(1'b1));  // open: _3__D0, _4__D1, _5__D2, _6__D3, _8__GND, _16__Vcc, _9__nPE
  _74162 u_74162_4 (
    ._1__nMR(nand_2_out), ._2__CP(nor_3_out), ._7__CEP(or_4_out), ._15__TC(n74162_4__15__tc),
    ._14__Q0(n74162_4__14__q0[0]), ._13__Q1(n74162_4__14__q0[1]), ._12__Q2(n74162_4__14__q0[2]),
    ._11__O3(n74162_4__14__q0[3]), ._10__CET(or_4_out));  // open: _3__D0, _4__D1, _5__D2, _6__D3, _8__GND, _16__Vcc, _9__nPE
  nor nor_3 (nor_3_out, and_5_out, nor_1_out);
  nand nand_3 (nand_3_out, n74162_5__14__q0[2], n74162_5__14__q0[0], n74162_6__15__tc);
  _74162 u_74162_5 (
    ._1__nMR(nand_3_out), ._2__CP(and_3_out), ._7__CEP(n74162_6__15__tc), ._14__Q0(n74162_5__14__q0[0]),
    ._13__Q1(n74162_5__14__q0[1]), ._12__Q2(n74162_5__14__q0[2]), ._11__O3(n74162_5__14__q0[3]),
    ._10__CET(n74162_6__15__tc));  // open: _3__D0, _4__D1, _5__D2, _6__D3, _8__GND, _16__Vcc, _15__TC, _9__nPE
  and and_8 (and_8_out, n74162_4__14__q0[0], n74162_4__14__q0[1], or_3_out);
  or or_3 (or_3_out, and_1_out, not_7_out);
  or or_4 (or_4_out, not_7_out, and_1_out);
  nand nand_4 (nand_4_out, n74162_7__14__q0[0], n74162_7__14__q0[2], n74162_8__15__tc);
  nor nor_4 (nor_4_out, nor_1_out, and_9_out);
  not not_7 (not_7_out, nand_4_out);
  Hex_Digit_Display hex_digit_display_3 (.value(multiplexer_3_out));  // open: dp
  Multiplexer #(.width(4), .enable("false")) multiplexer_3 (
    .in0(n74162_7__14__q0), .in1(n74162_5__14__q0), .out(multiplexer_3_out), .sel(t_ff_1_q));
  _74162 u_74162_6 (
    ._2__CP(and_3_out), ._7__CEP(1'b1), ._15__TC(n74162_6__15__tc), ._14__Q0(n74162_6__14__q0[0]),
    ._13__Q1(n74162_6__14__q0[1]), ._12__Q2(n74162_6__14__q0[2]), ._11__O3(n74162_6__14__q0[3]),
    ._10__CET(1'b1));  // open: _1__nMR, _3__D0, _4__D1, _5__D2, _6__D3, _8__GND, _16__Vcc, _9__nPE
  _74162 u_74162_7 (
    ._1__nMR(nand_4_out), ._2__CP(nor_4_out), ._7__CEP(or_5_out), ._14__Q0(n74162_7__14__q0[0]),
    ._13__Q1(n74162_7__14__q0[1]), ._12__Q2(n74162_7__14__q0[2]), ._11__O3(n74162_7__14__q0[3]),
    ._10__CET(or_5_out));  // open: _3__D0, _4__D1, _5__D2, _6__D3, _8__GND, _16__Vcc, _15__TC, _9__nPE
  and and_9 (and_9_out, and_6_out, n74162_8__15__tc);
  Hex_Digit_Display hex_digit_display_4 (.value(multiplexer_4_out));  // open: dp
  Multiplexer #(.width(4), .enable("false")) multiplexer_4 (
    .in0(n74162_8__14__q0), .in1(n74162_6__14__q0), .out(multiplexer_4_out), .sel(t_ff_1_q));
  or or_5 (or_5_out, n74162_8__15__tc, and_1_out);
  nor nor_5 (nor_5_out, and_6_out, nor_1_out);
  _74162 u_74162_8 (
    ._2__CP(nor_5_out), ._7__CEP(or_6_out), ._15__TC(n74162_8__15__tc), ._14__Q0(n74162_8__14__q0[0]),
    ._13__Q1(n74162_8__14__q0[1]), ._12__Q2(n74162_8__14__q0[2]), ._11__O3(n74162_8__14__q0[3]),
    ._10__CET(or_6_out));  // open: _1__nMR, _3__D0, _4__D1, _5__D2, _6__D3, _8__GND, _16__Vcc, _9__nPE
  or or_6 (or_6_out, not_9_out, and_1_out);
  _4bit_GLE u_4bit_gle_1 (
    .in_1(n74162_8__14__q0[3]), .in_2(n74162_8__14__q0[2]), .in_3(n74162_8__14__q0[1]),
    .in_4(n74162_8__14__q0[0]), .in_5(n74162_6__14__q0[3]), .in_6(n74162_6__14__q0[2]),
    .in_7(n74162_6__14__q0[1]), .in_8(n74162_6__14__q0[0]), .out_11(n4bit_gle_1_out_11));  // open: out_9, out_10
  and and_10 (and_10_out, n4bit_gle_1_out_11, n4bit_gle_2_out_11, n4bit_gle_3_out_11, n4bit_gle_4_out_11);
  nand nand_5 (nand_5_out, n74162_9__14__q0[2], n74162_9__14__q0[0], n74162_10__15__tc);
  not not_8 (not_8_out, and_7_out);
  not not_9 (not_9_out, nand_5_out);
  _4bit_GLE u_4bit_gle_2 (
    .in_1(n74162_7__14__q0[3]), .in_2(n74162_7__14__q0[2]), .in_3(n74162_7__14__q0[1]),
    .in_4(n74162_7__14__q0[0]), .in_5(n74162_5__14__q0[3]), .in_6(n74162_5__14__q0[2]),
    .in_7(n74162_5__14__q0[1]), .in_8(n74162_5__14__q0[0]), .out_11(n4bit_gle_2_out_11));  // open: out_9, out_10
  and and_11 (and_11_out, nand_5_out, not_8_out);
  nor nor_6 (nor_6_out, and_7_out, nor_1_out);
  Hex_Digit_Display hex_digit_display_5 (.value(multiplexer_5_out));  // open: dp
  Multiplexer #(.width(4), .enable("false")) multiplexer_5 (
    .in0(n74162_9__14__q0), .in1(4'b0000), .out(multiplexer_5_out), .sel(t_ff_1_q));
  _4bit_GLE u_4bit_gle_3 (
    .in_1(n74162_3__14__q0[3]), .in_2(n74162_3__14__q0[2]), .in_3(n74162_3__14__q0[1]),
    .in_4(n74162_3__14__q0[0]), .in_5(n74162_4__14__q0[3]), .in_6(n74162_4__14__q0[2]),
    .in_7(n74162_4__14__q0[1]), .in_8(n74162_4__14__q0[0]), .out_11(n4bit_gle_3_out_11));  // open: out_9, out_10
  _74162 u_74162_9 (
    ._1__nMR(and_11_out), ._2__CP(nor_6_out), ._7__CEP(n74162_10__15__tc), ._14__Q0(n74162_9__14__q0[0]),
    ._13__Q1(n74162_9__14__q0[1]), ._12__Q2(n74162_9__14__q0[2]), ._11__O3(n74162_9__14__q0[3]),
    ._10__CET(n74162_10__15__tc));  // open: _3__D0, _4__D1, _5__D2, _6__D3, _8__GND, _16__Vcc, _15__TC, _9__nPE
  not not_10 (not_10_out, and_7_out);
  Hex_Digit_Display hex_digit_display_6 (.value(multiplexer_6_out));  // open: dp
  Multiplexer #(.width(4), .enable("false")) multiplexer_6 (
    .in0(n74162_10__14__q0), .in1(4'b0000), .out(multiplexer_6_out), .sel(t_ff_1_q));
  _74162 u_74162_10 (
    ._1__nMR(not_10_out), ._2__CP(nor_7_out), ._7__CEP(1'b1), ._15__TC(n74162_10__15__tc),
    ._14__Q0(n74162_10__14__q0[0]), ._13__Q1(n74162_10__14__q0[1]), ._12__Q2(n74162_10__14__q0[2]),
    ._11__O3(n74162_10__14__q0[3]), ._10__CET(1'b1));  // open: _3__D0, _4__D1, _5__D2, _6__D3, _8__GND, _16__Vcc, _9__nPE
  nor nor_7 (nor_7_out, and_7_out, nor_1_out);
  _4bit_GLE u_4bit_gle_4 (
    .in_1(n74162_2__14__q0[3]), .in_2(n74162_2__14__q0[2]), .in_3(n74162_2__14__q0[1]),
    .in_4(n74162_2__14__q0[0]), .in_5(n74162_1__14__q0[3]), .in_6(n74162_1__14__q0[2]),
    .in_7(n74162_1__14__q0[1]), .in_8(n74162_1__14__q0[0]), .out_11(n4bit_gle_4_out_11));  // open: out_9, out_10

  // Notes on the sheet:
  //   알람 설정
  //   수정모드
  //   +1시간
  //   +1분
  //   0초
  //   1분동안 알람
endmodule

module _24hour_timer (
);

  wire and_1_out, and_2_out, and_3_out, and_4_out, and_5_out, and_6_out, and_7_out, and_8_out, button_1_out,
       button_2_out, button_3_out, button_4_out, clock_1_out, controlled_buffer_1_out, d_ff_1_q, d_ff_2_q,
       d_ff_3_q, d_ff_3_qn, d_ff_4_q, d_ff_4_qn, n74162_2__15__tc, n74162_4__15__tc, n74162_6__15__tc,
       nand_1_out, nand_2_out, nand_3_out, nor_1_out, nor_2_out, nor_3_out, nor_4_out, nor_5_out, nor_6_out,
       nor_7_out, not_1_out, not_2_out, not_3_out, not_4_out, not_5_out, not_6_out, not_7_out, not_8_out,
       or_1_out, or_2_out, or_3_out, or_4_out, or_5_out, xnor_1_out;
  wire [3:0] n74162_1__14__q0, n74162_2__14__q0, n74162_3__14__q0, n74162_4__14__q0, n74162_5__14__q0,
       n74162_6__14__q0;

  LED led_1 (.in(and_2_out));
  Clock clock_1 (.out(clock_1_out));
  assign controlled_buffer_1_out = not_2_out ? clock_1_out : 1'bz;  // Controlled_Buffer controlled_buffer_1
  Button button_1 (.out(button_1_out));
  not not_1 (not_1_out, nand_1_out);
  Button button_2 (.out(button_2_out));
  Button button_3 (.out(button_3_out));
  Button button_4 (.out(button_4_out));
  not not_2 (not_2_out, and_2_out);
  not not_3 (not_3_out, controlled_buffer_1_out);
  nand nand_1 (nand_1_out, n74162_1__14__q0[1], and_6_out);
  nor nor_1 (nor_1_out, not_1_out, and_1_out, nor_2_out);
  and and_1 (and_1_out, n74162_2__15__tc, and_3_out);
  nor nor_2 (nor_2_out, clock_1_out, and_2_out);
  and and_2 (and_2_out, xnor_1_out, d_ff_3_q);
  D_Flip_Flop #(.trigger("high")) d_ff_1 (.clk(not_4_out), .D(d_ff_3_qn), .Q(d_ff_1_q));  // open: Qn, preset, en, reset
  not not_4 (not_4_out, button_1_out);
  D_Flip_Flop #(.trigger("high")) d_ff_2 (.clk(not_3_out), .D(d_ff_4_qn), .Q(d_ff_2_q));  // open: Qn, preset, en, reset
  Hex_Digit_Display hex_digit_display_1 (.value(n74162_1__14__q0));  // open: dp
  Hex_Digit_Display hex_digit_display_2 (.value(n74162_2__14__q0));  // open: dp
  _74162 u_74162_1 (
    ._1__nMR(nand_1_out), ._2__CP(nor_1_out), ._7__CEP(or_1_out), ._14__Q0(n74162_1__14__q0[0]),
    ._13__Q1(n74162_1__14__q0[1]), ._12__Q2(n74162_1__14__q0[2]), ._11__O3(n74162_1__14__q0[3]),
    ._10__CET(or_1_out));  // open: _3__D0, _4__D1, _5__D2, _6__D3, _8__GND, _16__Vcc, _15__TC, _9__nPE
  or or_1 (or_1_out, n74162_2__15__tc, and_2_out);
  and and_3 (and_3_out, button_2_out, and_2_out);
  and and_4 (and_4_out, button_3_out, and_2_out);
  and and_5 (and_5_out, button_4_out, and_2_out);
  D_Flip_Flop #(.trigger("high")) d_ff_3 (
    .clk(button_1_out), .D(d_ff_1_q), .Q(d_ff_3_q), .Qn(d_ff_3_qn));  // open: preset, en, reset
  xnor xnor_1 (xnor_1_out, d_ff_2_q, d_ff_4_q);
  D_Flip_Flop #(.trigger("high")) d_ff_4 (
    .clk(controlled_buffer_1_out), .D(d_ff_2_q), .Q(d_ff_4_q), .Qn(d_ff_4_qn));  // open: preset, en, reset
  _74162 u_74162_2 (
    ._1__nMR(nand_1_out), ._2__CP(nor_3_out), ._7__CEP(or_3_out), ._15__TC(n74162_2__15__tc),
    ._14__Q0(n74162_2__14__q0[0]), ._13__Q1(n74162_2__14__q0[1]), ._12__Q2(n74162_2__14__q0[2]),
    ._11__O3(n74162_2__14__q0[3]), ._10__CET(or_3_out));  // open: _3__D0, _4__D1, _5__D2, _6__D3, _8__GND, _16__Vcc, _9__nPE
  nor nor_3 (nor_3_out, and_3_out, nor_2_out);
  and and_6 (and_6_out, n74162_2__14__q0[0], n74162_2__14__q0[1], or_2_out);
  or or_2 (or_2_out, and_2_out, not_5_out);
  or or_3 (or_3_out, not_5_out, and_2_out);
  nand nand_2 (nand_2_out, n74162_3__14__q0[0], n74162_3__14__q0[2], n74162_4__15__tc);
  nor nor_4 (nor_4_out, nor_2_out, and_7_out);
  not not_5 (not_5_out, nand_2_out);
  Hex_Digit_Display hex_digit_display_3 (.value(n74162_3__14__q0));  // open: dp
  _74162 u_74162_3 (
    ._1__nMR(nand_2_out), ._2__CP(nor_4_out), ._7__CEP(or_4_out), ._14__Q0(n74162_3__14__q0[0]),
    ._13__Q1(n74162_3__14__q0[1]), ._12__Q2(n74162_3__14__q0[2]), ._11__O3(n74162_3__14__q0[3]),
    ._10__CET(or_4_out));  // open: _3__D0, _4__D1, _5__D2, _6__D3, _8__GND, _16__Vcc, _15__TC, _9__nPE
  and and_7 (and_7_out, and_4_out, n74162_4__15__tc);
  Hex_Digit_Display hex_digit_display_4 (.value(n74162_4__14__q0));  // open: dp
  or or_4 (or_4_out, n74162_4__15__tc, and_2_out);
  nor nor_5 (nor_5_out, and_4_out, nor_2_out);
  _74162 u_74162_4 (
    ._2__CP(nor_5_out), ._7__CEP(or_5_out), ._15__TC(n74162_4__15__tc), ._14__Q0(n74162_4__14__q0[0]),
    ._13__Q1(n74162_4__14__q0[1]), ._12__Q2(n74162_4__14__q0[2]), ._11__O3(n74162_4__14__q0[3]),
    ._10__CET(or_5_out));  // open: _1__nMR, _3__D0, _4__D1, _5__D2, _6__D3, _8__GND, _16__Vcc, _9__nPE
  or or_5 (or_5_out, not_7_out, and_2_out);
  nand nand_3 (nand_3_out, n74162_5__14__q0[2], n74162_5__14__q0[0], n74162_6__15__tc);
  not not_6 (not_6_out, and_5_out);
  not not_7 (not_7_out, nand_3_out);
  and and_8 (and_8_out, nand_3_out, not_6_out);
  nor nor_6 (nor_6_out, and_5_out, nor_2_out);
  Hex_Digit_Display hex_digit_display_5 (.value(n74162_5__14__q0));  // open: dp
  _74162 u_74162_5 (
    ._1__nMR(and_8_out), ._2__CP(nor_6_out), ._7__CEP(n74162_6__15__tc), ._14__Q0(n74162_5__14__q0[0]),
    ._13__Q1(n74162_5__14__q0[1]), ._12__Q2(n74162_5__14__q0[2]), ._11__O3(n74162_5__14__q0[3]),
    ._10__CET(n74162_6__15__tc));  // open: _3__D0, _4__D1, _5__D2, _6__D3, _8__GND, _16__Vcc, _15__TC, _9__nPE
  not not_8 (not_8_out, and_5_out);
  Hex_Digit_Display hex_digit_display_6 (.value(n74162_6__14__q0));  // open: dp
  _74162 u_74162_6 (
    ._1__nMR(not_8_out), ._2__CP(nor_7_out), ._7__CEP(1'b1), ._15__TC(n74162_6__15__tc),
    ._14__Q0(n74162_6__14__q0[0]), ._13__Q1(n74162_6__14__q0[1]), ._12__Q2(n74162_6__14__q0[2]),
    ._11__O3(n74162_6__14__q0[3]), ._10__CET(1'b1));  // open: _3__D0, _4__D1, _5__D2, _6__D3, _8__GND, _16__Vcc, _9__nPE
  nor nor_7 (nor_7_out, and_5_out, nor_2_out);

  // Notes on the sheet:
  //   수정모드
  //   Set Sec 0
  //   +1Hour
  //   +1Min
endmodule

module \알람_시간설정  (
);

  wire button_1_out, button_2_out, n74162_2__15__tc, n74162_4__15__tc, nand_1_out, nand_2_out;
  wire [3:0] n74162_1__14__q0, n74162_2__14__q0, n74162_3__14__q0, n74162_4__14__q0;

  Button button_1 (.out(button_1_out));
  Button button_2 (.out(button_2_out));
  Hex_Digit_Display hex_digit_display_1 (.value(n74162_1__14__q0));  // open: dp
  nand nand_1 (nand_1_out, n74162_2__14__q0[0], n74162_2__14__q0[1], n74162_1__14__q0[1]);
  _74162 u_74162_1 (
    ._1__nMR(nand_1_out), ._2__CP(button_1_out), ._7__CEP(n74162_2__15__tc), ._14__Q0(n74162_1__14__q0[0]),
    ._13__Q1(n74162_1__14__q0[1]), ._12__Q2(n74162_1__14__q0[2]), ._11__O3(n74162_1__14__q0[3]),
    ._10__CET(n74162_2__15__tc));  // open: _3__D0, _4__D1, _5__D2, _6__D3, _8__GND, _16__Vcc, _15__TC, _9__nPE
  Hex_Digit_Display hex_digit_display_2 (.value(n74162_2__14__q0));  // open: dp
  nand nand_2 (nand_2_out, n74162_3__14__q0[2], n74162_3__14__q0[0], n74162_4__15__tc);
  _74162 u_74162_2 (
    ._1__nMR(nand_1_out), ._2__CP(button_1_out), ._7__CEP(1'b1), ._15__TC(n74162_2__15__tc),
    ._14__Q0(n74162_2__14__q0[0]), ._13__Q1(n74162_2__14__q0[1]), ._12__Q2(n74162_2__14__q0[2]),
    ._11__O3(n74162_2__14__q0[3]), ._10__CET(1'b1));  // open: _3__D0, _4__D1, _5__D2, _6__D3, _8__GND, _16__Vcc, _9__nPE
  Hex_Digit_Display hex_digit_display_3 (.value(n74162_3__14__q0));  // open: dp
  _74162 u_74162_3 (
    ._1__nMR(nand_2_out), ._2__CP(button_2_out), ._7__CEP(n74162_4__15__tc), ._14__Q0(n74162_3__14__q0[0]),
    ._13__Q1(n74162_3__14__q0[1]), ._12__Q2(n74162_3__14__q0[2]), ._11__O3(n74162_3__14__q0[3]),
    ._10__CET(n74162_4__15__tc));  // open: _3__D0, _4__D1, _5__D2, _6__D3, _8__GND, _16__Vcc, _15__TC, _9__nPE
  Hex_Digit_Display hex_digit_display_4 (.value(n74162_4__14__q0));  // open: dp
  _74162 u_74162_4 (
    ._2__CP(button_2_out), ._7__CEP(1'b1), ._15__TC(n74162_4__15__tc), ._14__Q0(n74162_4__14__q0[0]),
    ._13__Q1(n74162_4__14__q0[1]), ._12__Q2(n74162_4__14__q0[2]), ._11__O3(n74162_4__14__q0[3]),
    ._10__CET(1'b1));  // open: _1__nMR, _3__D0, _4__D1, _5__D2, _6__D3, _8__GND, _16__Vcc, _9__nPE
endmodule

module _1bit_GLE (
  input  in_1,
  input  in_2,
  input  in_3,
  input  in_4,
  input  in_5,
  output out_6,
  output out_7,
  output out_8
);

  wire and_1_out, and_2_out, not_1_out, not_2_out, xnor_1_out;

  xnor xnor_1 (xnor_1_out, in_1, in_2);
  not not_1 (not_1_out, in_2);
  and and_1 (and_1_out, in_5, in_1, not_1_out);
  not not_2 (not_2_out, in_1);
  and and_2 (and_2_out, in_5, not_2_out, in_2);
  or or_1 (out_6, and_1_out, in_3);
  or or_2 (out_7, and_2_out, in_4);
  and and_3 (out_8, xnor_1_out, in_5);
endmodule

module _4bit_GLE (
  input  in_1,
  input  in_2,
  input  in_3,
  input  in_4,
  input  in_5,
  input  in_6,
  input  in_7,
  input  in_8,
  output out_9,
  output out_10,
  output out_11
);

  wire n1bit_gle_1_out_6, n1bit_gle_1_out_7, n1bit_gle_1_out_8, n1bit_gle_2_out_6, n1bit_gle_2_out_7,
       n1bit_gle_2_out_8, n1bit_gle_3_out_6, n1bit_gle_3_out_7, n1bit_gle_3_out_8;

  _1bit_GLE u_1bit_gle_1 (
    .in_3(1'b0), .in_4(1'b0), .in_5(1'b1), .in_1(in_1), .in_2(in_5), .out_6(n1bit_gle_1_out_6),
    .out_7(n1bit_gle_1_out_7), .out_8(n1bit_gle_1_out_8));
  _1bit_GLE u_1bit_gle_2 (
    .in_3(n1bit_gle_1_out_6), .in_4(n1bit_gle_1_out_7), .in_5(n1bit_gle_1_out_8), .in_1(in_2), .in_2(in_6),
    .out_6(n1bit_gle_2_out_6), .out_7(n1bit_gle_2_out_7), .out_8(n1bit_gle_2_out_8));
  _1bit_GLE u_1bit_gle_3 (
    .in_3(n1bit_gle_2_out_6), .in_4(n1bit_gle_2_out_7), .in_5(n1bit_gle_2_out_8), .in_1(in_3), .in_2(in_7),
    .out_6(n1bit_gle_3_out_6), .out_7(n1bit_gle_3_out_7), .out_8(n1bit_gle_3_out_8));
  _1bit_GLE u_1bit_gle_4 (
    .in_3(n1bit_gle_3_out_6), .in_4(n1bit_gle_3_out_7), .in_5(n1bit_gle_3_out_8), .in_1(in_4), .in_2(in_8),
    .out_6(out_9), .out_7(out_10), .out_8(out_11));
endmodule
