// Logisim project 카운터.circ as structural Verilog: 1 circuit, main circuit main
module main (
  input  in_1
);

  wire and_1_out, and_2_out, button_1_out, decoder_1_out0, decoder_1_out1, decoder_1_out2, decoder_1_out3,
       decoder_1_out4, decoder_1_out5, decoder_1_out6, decoder_1_out7, j_k_ff_2_qn, j_k_ff_3_qn, not_1_out,
       or_1_out, xor_1_out;
  wire [2:0] j_k_ff_3_q;

  not not_1 (not_1_out, in_1);
  and and_1 (and_1_out, in_1, j_k_ff_2_qn, j_k_ff_3_qn);
  or or_1 (or_1_out, and_1_out, and_2_out);
  and and_2 (and_2_out, not_1_out, j_k_ff_3_q[0], j_k_ff_3_q[1]);
  xor xor_1 (xor_1_out, in_1, j_k_ff_3_q[0]);
  Button button_1 (.out(button_1_out));
  J_K_Flip_Flop j_k_ff_1 (
    .J(or_1_out), .clk(button_1_out), .K(or_1_out), .Q(j_k_ff_3_q[2]));  // open: Qn, preset, en, reset
  J_K_Flip_Flop j_k_ff_2 (
    .J(xor_1_out), .clk(button_1_out), .K(xor_1_out), .Q(j_k_ff_3_q[1]), .Qn(j_k_ff_2_qn));  // open: preset, en, reset
  J_K_Flip_Flop j_k_ff_3 (
    .J(1'b1), .clk(button_1_out), .K(1'b1), .Q(j_k_ff_3_q[0]), .Qn(j_k_ff_3_qn));  // open: preset, en, reset
  Hex_Digit_Display hex_digit_display_1 (.value({1'b0, j_k_ff_3_q}));  // open: dp
  Decoder #(.select(3), .enable("false")) decoder_1 (
    .out0(decoder_1_out0), .out1(decoder_1_out1), .out2(decoder_1_out2), .out3(decoder_1_out3),
    .out4(decoder_1_out4), .out5(decoder_1_out5), .out6(decoder_1_out6), .out7(decoder_1_out7),
    .sel(j_k_ff_3_q));
  LED led_1 (.in(decoder_1_out0));
  LED led_2 (.in(decoder_1_out1));
  LED led_3 (.in(decoder_1_out2));
  LED led_4 (.in(decoder_1_out3));
  LED led_5 (.in(decoder_1_out4));
  LED led_6 (.in(decoder_1_out5));
  LED led_7 (.in(decoder_1_out6));
  LED led_8 (.in(decoder_1_out7));
endmodule
