// Logisim project 카운터들.circ as structural Verilog: 1 circuit, main circuit main
module main (
  input  in_1,
  input  in_2
);

  wire and_1_out, clock_1_out, clock_2_out, d_ff_1_q, d_ff_2_q, d_ff_3_q, d_ff_4_qn, not_1_out;
  wire [3:0] n74163_1__14__q0;

  Clock clock_1 (.out(clock_1_out));
  LED led_1 (.in(d_ff_1_q));
  D_Flip_Flop d_ff_1 (.clk(clock_1_out), .D(d_ff_4_qn), .Q(d_ff_1_q), .reset(in_1));  // open: Qn, preset, en
  Clock clock_2 (.out(clock_2_out));
  D_Flip_Flop d_ff_2 (.clk(clock_1_out), .D(d_ff_1_q), .Q(d_ff_2_q), .reset(in_1));  // open: Qn, preset, en
  not not_1 (not_1_out, and_1_out);
  _74163 u_74163_1 (
    ._1__nMR(in_2), ._2__CP(clock_2_out), ._7__CEP(not_1_out), ._14__Q0(n74163_1__14__q0[0]),
    ._13__Q1(n74163_1__14__q0[1]), ._12__Q2(n74163_1__14__q0[2]), ._11__O3(n74163_1__14__q0[3]),
    ._10__CET(in_2));  // open: _3__D0, _4__D1, _5__D2, _6__D3, _8__GND, _16__Vcc, _15__TC, _9__nPE
  LED led_2 (.in(d_ff_2_q));
  D_Flip_Flop d_ff_3 (.clk(clock_1_out), .D(d_ff_2_q), .Q(d_ff_3_q), .reset(in_1));  // open: Qn, preset, en
  LED led_3 (.in(and_1_out));
  and and_1 (and_1_out, n74163_1__14__q0[3], n74163_1__14__q0[2], n74163_1__14__q0[0]);
  LED led_4 (.in(d_ff_3_q));
  Hex_Digit_Display hex_digit_display_1 (.value(n74163_1__14__q0));  // open: dp
  LED led_5 (.in(d_ff_4_qn));
  D_Flip_Flop d_ff_4 (.clk(clock_1_out), .D(d_ff_3_q), .Qn(d_ff_4_qn), .reset(in_1));  // open: Q, preset, en
endmodule
